// Logisim project calculator.circ as structural Verilog
module main (
);

  wire w0, w1, w2, w3, w4, w5, w6, w7, w8, w9;
  wire [15:0] QAReg, shifter_1_out;

  Register #(.width(4)) register_1 ();  // open: D, en, Q, clk, clr
  Button button_1 (.out(w7));
  Button button_2 (.out(w4));
  Button button_3 (.out(w1));
  Button button_4 (.out(w0));
  Register #(.width(4)) register_2 ();  // open: D, en, Q, clk, clr
  Button button_5 (.out(w8));
  Button button_6 (.out(w5));
  Button button_7 (.out(w2));
  Button button_8 (.out(w9));
  Button button_9 (.out(w6));
  Button button_10 (.out(w3));
  Register #(.width(4)) register_3 ();  // open: D, en, Q, clk, clr
  Register #(.width(4)) register_4 ();  // open: D, en, Q, clk, clr
  Shifter #(.width(16)) shifter_1 (.in(QAReg), .\dist (4'b0001), .out(shifter_1_out));
  Register #(.width(16)) register_5 (.Q(QAReg));  // open: D, en, clk, clr
  Register #(.width(4)) register_6 ();  // open: D, en, Q, clk, clr
  Adder #(.width(16)) adder_1 (.a(shifter_1_out));  // open: b, out, cin, cout
endmodule
